# Fritzing sketch sketch (saved by Fritzing 0.9.2b)
breadboards: 1

parts:
  OLED = Grove OLED 128x96
  U1 = ENCODER_2LED [package=encoder_led_2]
  Part1 = Arduino Nano (Rev3.0) (ICSP)
  Q1 = Basic FET N-Channel [package="DPak [SMD]"]
  LED1 = LEDs [package=led10mm]
  Power_plug1 = Power plug
  Q2 = TRANSISTOR_NPN [package=to-92]
  R1 = Resistor [tolerance=±5% resistance=10k package="1206 [SMD]"]
  R2 = Resistor [tolerance=±5% resistance=1k package="1206 [SMD]"]

nets:
  GND: OLED.GND, U1.-, Q1.source, Power_plug1.GND, R1.Pin_0
  VCC: OLED.VCC, Part1.VIN
  N1: OLED.SDA, Part1.A4
  N2: OLED.SCL, Part1.A5
  N3: U1.+G, Part1.D2
  N4: U1.+R, Part1.D3
  N5: U1.SW, Part1.D4
  N6: Part1.D10, R2.Pin_0
  N7: Q1.Gate, Q2.E, R1.Pin_1
  N8: Q1.drain, LED1.C
  N9: LED1.A, Power_plug1.VCC, Q2.C
  N10: Q2.B, R2.Pin_1
